# Fritzing sketch circuit connection (saved by Fritzing 0.9.2b)
breadboards: 1

parts:
  R1 = Resistor [tolerance=±5% resistance=220 package="2512 [SMD]"]
  Part1 = Arduino Uno (Rev3) - ICSP
  LED1 = smd LED [color="Red (633nm)" package="1206 [SMD]"]
  FC-1 = Sound Sensor

nets:
  N1: R1.Pin_0, Part1.D4
  N2: R1.Pin_1, LED1.anode
  N3: Part1.D6_PWM, FC-1.OUT
  5V: Part1.5V, FC-1.VCC
  GND: Part1.GND, LED1.cathode, FC-1.GND
